// Logisim project ALU.circ as structural Verilog: 9 circuits, main circuit main
module main (
  input  [3:0] A,
  input  [3:0] B,
  input  [3:0] OP,
  output [3:0] R,
  output Z_Flag,
  output S_Flag,
  output C_Flag
);

  wire [3:0] ALU_ADD_SUB, ALU_AND, ALU_LOR, ALU_NOT, ALU_OR, ALU_ROR, ALU_XOR;

  // NoConnect on B[2]
  // NoConnect on B[3]
  ALU_AND alu_and_1 (.A(A), .B(B), .O(ALU_AND));
  ALU_OR alu_or_1 (.A(A), .B(B), .O(ALU_OR));
  ALU_XOR alu_xor_1 (.A(A), .B(B), .O(ALU_XOR));
  ALU_NOT alu_not_1 (.A(A), .O(ALU_NOT));
  ALU_LOR alu_lor_1 (.A(A), .Shift(B[1:0]), .O(ALU_LOR));
  ALU_ROR alu_ror_1 (.A(A), .Shift(B[1:0]), .O(ALU_ROR));
  ADD_SUB add_sub_1 (.Sel(OP[0]), .A(A), .B(B), .Carry(C_Flag), .O(ALU_ADD_SUB));
  // NoConnect on OP[1]
  // NoConnect on OP[2]
  // NoConnect on OP[3]
  Multiplexer #(.select(4), .width(4)) multiplexer_1 (
    .in0(ALU_AND), .in1(ALU_OR), .in2(ALU_XOR), .in3(ALU_LOR), .in4(ALU_ROR), .in5(ALU_NOT),
    .in6(ALU_ADD_SUB), .in7(ALU_ADD_SUB), .out(R), .sel(OP));  // open: in8, in9, in10, in11, in12, in13, in14, in15
  nor nor_1 (Z_Flag, R[0], R[1], R[2], R[3]);

  assign S_Flag = R[3];

  // Other names for the same wires on the sheet: S0 = B[0]; Shift[1:0] = B[1:0]; S1 = B[1]; SEL = OP[0]
endmodule

module FA (
  input  a,
  input  b,
  input  Cin,
  output S,
  output Cout
);

  wire and_1_out, and_2_out, xor_1_out;

  xor xor_1 (xor_1_out, a, b);
  xor xor_2 (S, xor_1_out, Cin);
  and and_1 (and_1_out, Cin, xor_1_out);
  and and_2 (and_2_out, a, b);
  or or_1 (Cout, and_1_out, and_2_out);
endmodule

module ALU_AND (
  input  [3:0] A,
  input  [3:0] B,
  output [3:0] O
);

  and and_1 (O[3], A[3], B[3]);
  and and_2 (O[2], A[2], B[2]);
  and and_3 (O[1], A[1], B[1]);
  and and_4 (O[0], A[0], B[0]);
endmodule

module ALU_OR (
  input  [3:0] A,
  input  [3:0] B,
  output [3:0] O
);

  or or_1 (O[3], A[3], B[3]);
  or or_2 (O[2], A[2], B[2]);
  or or_3 (O[1], A[1], B[1]);
  or or_4 (O[0], A[0], B[0]);
endmodule

module ALU_XOR (
  input  [3:0] A,
  input  [3:0] B,
  output [3:0] O
);

  xor xor_1 (O[3], A[3], B[3]);
  xor xor_2 (O[2], A[2], B[2]);
  xor xor_3 (O[1], A[1], B[1]);
  xor xor_4 (O[0], A[0], B[0]);
endmodule

module ALU_NOT (
  input  [3:0] A,
  output [3:0] O
);

  not not_1 (O[3], A[3]);
  not not_2 (O[2], A[2]);
  not not_3 (O[1], A[1]);
  not not_4 (O[0], A[0]);
endmodule

module ALU_LOR (
  input  [3:0] A,
  input  [1:0] Shift,
  output [3:0] O
);

  Multiplexer #(.select(2)) multiplexer_1 (.in0(A[3]), .in1(A[2]), .in2(A[1]), .in3(A[0]), .out(O[3]), .sel(Shift));
  Multiplexer #(.select(2)) multiplexer_2 (.in0(A[2]), .in1(A[1]), .in2(A[0]), .in3(A[3]), .out(O[2]), .sel(Shift));
  Multiplexer #(.select(2)) multiplexer_3 (.in0(A[1]), .in1(A[0]), .in2(A[3]), .in3(A[2]), .out(O[1]), .sel(Shift));
  Multiplexer #(.select(2)) multiplexer_4 (.in0(A[0]), .in1(A[3]), .in2(A[2]), .in3(A[1]), .out(O[0]), .sel(Shift));

  // Notes on the sheet:
  //   Left Rotate Circuit
endmodule

module ALU_ROR (
  input  [3:0] A,
  input  [1:0] Shift,
  output [3:0] O
);

  Multiplexer #(.select(2)) multiplexer_1 (.in0(A[3]), .in1(A[0]), .in2(A[1]), .in3(A[2]), .out(O[3]), .sel(Shift));
  Multiplexer #(.select(2)) multiplexer_2 (.in0(A[2]), .in1(A[3]), .in2(A[0]), .in3(A[1]), .out(O[2]), .sel(Shift));
  Multiplexer #(.select(2)) multiplexer_3 (.in0(A[1]), .in1(A[2]), .in2(A[3]), .in3(A[0]), .out(O[1]), .sel(Shift));
  Multiplexer #(.select(2)) multiplexer_4 (.in0(A[0]), .in1(A[1]), .in2(A[2]), .in3(A[3]), .out(O[0]), .sel(Shift));

  // Notes on the sheet:
  //   Right Rotate Circuit
endmodule

module ADD_SUB (
  input  Sel,
  input  [3:0] A,
  input  [3:0] B,
  output Carry,
  output [3:0] O
);

  wire fa_1_cout, fa_2_cout, fa_3_cout, xor_1_out, xor_2_out, xor_3_out, xor_4_out;

  xor xor_1 (xor_1_out, B[0], Sel);
  FA fa_1 (.a(A[0]), .b(xor_1_out), .Cin(Sel), .S(O[0]), .Cout(fa_1_cout));
  xor xor_2 (xor_2_out, B[1], Sel);
  FA fa_2 (.a(A[1]), .b(xor_2_out), .Cin(fa_1_cout), .S(O[1]), .Cout(fa_2_cout));
  xor xor_3 (xor_3_out, B[2], Sel);
  FA fa_3 (.a(A[2]), .b(xor_3_out), .Cin(fa_2_cout), .S(O[2]), .Cout(fa_3_cout));
  xor xor_4 (xor_4_out, B[3], Sel);
  FA fa_4 (.a(A[3]), .b(xor_4_out), .Cin(fa_3_cout), .S(O[3]), .Cout(Carry));
endmodule
